# Fritzing sketch ClusterArdyno (saved by Fritzing 0.9.9b)
circuit board: 5.16197cm x 3.52549cm
breadboards: 1

parts:
  R1 = Resistor [tolerance=±5% power=0.25 resistance=470 package=THT]
  C1 = Electrolytic Capacitor [capacitance=10µF voltage=35V package="100 mil [THT, electrolytic]"]
  C3 = Electrolytic Capacitor [capacitance=1µF voltage=35V package="100 mil [THT, electrolytic]"]
  R2 = Resistor [tolerance=±5% power=0.25 resistance=1000 package=THT]
  R3 = Resistor [tolerance=±5% power=0.25 resistance=18k package=THT]
  C5 = Ceramic Capacitor [capacitance=100nF voltage=35V package="100 mil [THT, multilayer]"]
  R4 = Resistor [tolerance=±5% power=0.25 resistance=10k package=THT]
  C6 = Ceramic Capacitor [capacitance=100pF voltage=35V package="100 mil [THT, multilayer]"]
  D1 = Diode [package=diode-1n4148]
  R5 = Resistor [tolerance=±5% power=0.25 resistance=100k package=THT]
  LED1 = LED - 5mm [color="Blue (525nm)" current=0.030 package="5 mm [THT]"]
  R6 = Resistor [tolerance=±5% power=0.25 resistance=1k package=THT]
  C7 = Ceramic Capacitor [capacitance=3pF voltage=35V package="100 mil [THT, multilayer]"]
  JP2 = Header 2 [package=jst-2-pth-ns]
  JP1 = Header 2 [package=jst-2-pth]
  U1 = 555 Timer [package="DIP8 [THT]"]
  RPMTempSensorv0_9 = Arduino Nano (Rev3.0) (ICSP)
  C8 = Ceramic Capacitor [capacitance=100nF voltage=35V package="100 mil [THT, multilayer]"]
  BC547 = TRANSISTOR_NPN_2 [package=to-92]
  C9 = Ceramic Capacitor [capacitance=100nF voltage=35V package="100 mil [THT, multilayer]"]

nets:
  N1: R1.Pin_0, C1.+, C3.+, R3.Pin_0, R4.Pin_0, JP2.2, U1.Reset, U1.Vcc_Supply_Voltage, RPMTempSensorv0_9.5V, C8.0
  N2: R1.Pin_1, LED1.anode
  GND: C1.-, C3.-, C5.0, D1.A, R5.Pin_1, LED1.cathode, R6.Pin_1, JP1.1, U1.Ground, RPMTempSensorv0_9.GND, C8.1, BC547.E, C9.1
  N3: R2.Pin_0, U1.Output
  N4: R2.Pin_1, RPMTempSensorv0_9.D3
  N5: R3.Pin_1, U1.Threshold, U1.Discharge, C9.0
  N6: C5.1, U1.Control_Voltage
  N7: R4.Pin_1, U1.Trigger, BC547.C
  N8: C6.0, C7.1
  N9: C6.1, D1.C, R5.Pin_0, BC547.B
  N10: R6.Pin_0, JP2.1, RPMTempSensorv0_9.A1
  N11: C7.0, JP1.2
